# Fritzing sketch schema (saved by Fritzing 0.8.5b)
stripboards: 1

parts:
  J1 = male pin header, 6 pins [form="♂ (male)"]
  J2 = male pin header, 6 pins [form="♂ (male)"]
  J3 = male pin header, 6 pins [form="♂ (male)"]
  J4 = male pin header, 7 pins [form="♂ (male)"]
  J5 = male pin header, 7 pins [form="♂ (male)"]
  J6 = male pin header, 11 pins [form="♂ (male)"]
  J7 = male pin header, 1 pin [form="♂ (male)"]
  J8 = male pin header, 1 pin [form="♂ (male)"]
  Q1 = NPN-Transistor [package="TO92 [THT]"]
  R1 = Resistor [tolerance=±5% package="2512 [SMD]"]
  R2 = Resistor [tolerance=±5% package="2512 [SMD]"]
  R3 = Resistor [tolerance=±5% package="2512 [SMD]"]
  R4 = Resistor [tolerance=±5% package="2512 [SMD]"]
  R5 = Resistor [tolerance=±5% package="2512 [SMD]"]
  R6 = Resistor [tolerance=±5% package="2512 [SMD]"]
  R7 = Resistor [tolerance=±5% package="2512 [SMD]"]
  R8 = Resistor [tolerance=±5% package="2512 [SMD]"]
  R9 = Resistor [tolerance=±5% package="2512 [SMD]"]
  R10 = Resistor [tolerance=±5% package="2512 [SMD]"]
  R11 = Resistor [tolerance=±5% package="2512 [SMD]"]
  R12 = Resistor [tolerance=±5% package="2512 [SMD]"]
  R13 = Resistor [tolerance=±5% package="2512 [SMD]"]

nets:
  N1: J1.pin1, J1.pin2, J1.pin3, J1.pin4, J1.pin5, J1.pin6, J6.pin11, R1.Pin_0, R2.Pin_0, R3.Pin_0, R4.Pin_0, R5.Pin_0, R6.Pin_0, R7.Pin_0
  N2: J2.pin1, J3.pin1, R13.Pin_1
  N3: J2.pin2, J3.pin2, R8.Pin_1
  N4: J2.pin3, J3.pin3, R9.Pin_1
  N5: J2.pin4, J3.pin4, R10.Pin_1
  N6: J2.pin5, J3.pin5, R12.Pin_1
  N7: J2.pin6, J3.pin6, R11.Pin_1
  N8: J4.pin1, R1.Pin_1
  N9: J4.pin2, R7.Pin_1
  N10: J4.pin3, R6.Pin_1
  N11: J4.pin4, R5.Pin_1
  N12: J4.pin5, R3.Pin_1
  N13: J4.pin6, R4.Pin_1
  N14: J4.pin7, R2.Pin_1
  N15: J5.pin1, J6.pin3
  N16: J5.pin2, J6.pin4
  N17: J5.pin3, J6.pin5
  N18: J5.pin4, J6.pin6
  N19: J5.pin5, J6.pin7
  N20: J5.pin6, J6.pin8
  N21: J5.pin7, J6.pin9
  N22: J6.pin1, Q1.B
  N23: J7.pin1, R8.Pin_0, R9.Pin_0, R10.Pin_0, R11.Pin_0, R12.Pin_0, R13.Pin_0
  N24: J8.pin1, Q1.E
